# Fritzing sketch Untitled Sketch (saved by Fritzing 0.9.3b)
breadboards: 1

parts:
  R1 = Resistor [tolerance=±5% resistance=220 package=THT]
  LED1 = LED - 5mm [color="Red (633nm)" package="5 mm [THT]"]
  Componente1 = Lilypad Power Supply

nets:
  N1: R1.Pin_0, R1.Pin_1, LED1.cathode, LED1.anode, Componente1.GND

notes:
  R1
  D1
  BAT1
